# Fritzing sketch iLuminator (saved by Fritzing 0.9.3b)

parts:
  Part1 = Arduino Micro (Rev3)  # not connected
  Part2 = FemtoBuck LED Driver
  R1 = Rotary Potentiometer (Large) [maximum_resistance=100kΩ package=THT]
  IC1 = iLuminator Board [chip_label="iLuminator Board" package="DIP (Dual Inline) [THT]"]
  LED1 = LED - 5mm [color="Red (633nm)" package="5 mm [THT]"]

nets:
  N1: Part2.PGND, IC1.pin8
  N2: Part2.VIN, IC1.pin7
  N3: Part2.D-, IC1.pin6
  N4: Part2.D+, IC1.pin5
  N5: Part2.OUT+, IC1.pin3
  N6: Part2.OUT-, IC1.pin4
  N7: R1.leg1, IC1.pin11
  N8: R1.wiper, IC1.pin10
  N9: R1.leg2, IC1.pin9
  N10: IC1.pin1, LED1.cathode
  N11: IC1.pin2, LED1.anode

custom parts:
  iLuminator Board: Board for Clubes de Ciencia Mexico's iLuminator assembly
